// Logisim project Projet.circ as structural Verilog
module Add8bits (
  input  [7:0] in_1,
  input  [7:0] in_2,
  output [7:0] out_3,
  output ZF,
  output CF,
  output SF,
  output OF
);

  wire and_1_out, and_2_out, comparator_1_lt, comparator_2_lt, not_1_out, not_2_out, not_3_out, or_1_out;

  Adder adder_1 (.a(in_1), .b(in_2), .out(out_3));  // open: cin, cout
  Subtractor subtractor_1 (.a(in_1), .b(in_2), .out(out_3));  // open: bin, bout
  not not_1 (not_1_out, in_2[7]);
  not not_2 (not_2_out, in_1[7]);
  // NOT_Gate not_3 has open pins: in=open, out=not_3_out
  Comparator comparator_1 (.a(out_3), .b(in_1), .lt(comparator_1_lt));  // open: gt, eq
  Comparator comparator_2 (.a(out_3), .b(in_2), .lt(comparator_2_lt));  // open: gt, eq
  and and_1 (and_1_out, in_2[7], not_3_out, in_1[7]);
  and and_2 (and_2_out, not_1_out, not_2_out);
  not not_4 (ZF, or_1_out);
  or or_1 (or_1_out, out_3[0], out_3[1], out_3[2], out_3[3], out_3[4], out_3[5], out_3[6], out_3[7]);
  or or_2 (OF, and_1_out, and_2_out);
  or or_3 (CF, comparator_1_lt, comparator_2_lt);
  not not_5 (SF, 1'b1);
endmodule

module Soustracteur8bits (
  input  [7:0] in_1,
  input  [7:0] in_2,
  output [7:0] out_3
);

  Subtractor subtractor_1 (.a(in_1), .b(in_2), .out(out_3));  // open: bin, bout
endmodule

module OU8bits (
  input  [7:0] in_1,
  input  [7:0] in_2,
  output [7:0] out_3,
  output ZF
);

  wire or_2_out;
  wire [7:0] subtractor_1_out;

  assign out_3 = in_1 | in_2;  // OR_Gate or_1, 8 bits wide
  Subtractor subtractor_1 (.a(in_1), .b(in_2), .out(subtractor_1_out));  // open: bin, bout
  or or_2 (or_2_out, subtractor_1_out[0], subtractor_1_out[1], subtractor_1_out[2], subtractor_1_out[3], subtractor_1_out[4], subtractor_1_out[5], subtractor_1_out[6], subtractor_1_out[7]);
  not not_1 (ZF, or_2_out);
endmodule

module UAL (
  input  [7:0] RS,
  input  [7:0] RT,
  input  [2:0] in_3,
  output CF,
  output ZF,
  output SF,
  output OF,
  output [7:0] out_8
);

  wire and_1_out, and_2_out, and_3_out, and_5_out;
  wire [7:0] adder_1_out, and_4_out, not_1_out, or_1_out, shifter_1_out, shifter_2_out, subtractor_1_out;

  Subtractor subtractor_1 (.a(RS), .b(RT), .out(subtractor_1_out));  // open: bin, bout
  Adder adder_1 (.a(RS), .b(RT), .out(adder_1_out), .cout(CF));  // open: cin
  and and_1 (and_1_out, ~out_8[7], RS[7], ~RT[7], in_3[0]);  // AND_Gate
  assign or_1_out = RT | RS;  // OR_Gate or_1, 8 bits wide
  and and_2 (and_2_out, ~out_8[7], RS[7], RT[7], ~in_3[0]);  // AND_Gate
  Multiplexer #(.select(3), .width(8)) multiplexer_1 (
    .in0(adder_1_out), .in1(subtractor_1_out), .in2(or_1_out), .in3(and_4_out), .in4(not_1_out),
    .in5(shifter_1_out), .in6(shifter_2_out), .out(out_8), .sel(in_3));  // open: in7, en
  and and_3 (and_3_out, out_8[7], ~RS[7], ~RT[7], ~in_3[0]);  // AND_Gate
  or or_2 (OF, and_1_out, and_2_out, and_3_out, and_5_out);
  assign not_1_out = ~RS;  // NOT_Gate not_1, 8 bits wide
  assign and_4_out = RT & RS;  // AND_Gate and_4, 8 bits wide
  and and_5 (and_5_out, out_8[7], ~RS[7], RT[7], in_3[0]);  // AND_Gate
  Shifter shifter_1 (.in(RS), .\dist (RT[2:0]), .out(shifter_1_out));
  Shifter #(.shift("lr")) shifter_2 (.in(RS), .\dist (RT[2:0]), .out(shifter_2_out));
  and and_6 (ZF, ~out_8[0], ~out_8[1], ~out_8[2], ~out_8[3], ~out_8[4], ~out_8[5], ~out_8[6], ~out_8[7]);  // AND_Gate

  assign SF = out_8[7];
endmodule

module decoder_instru (
  input  [3:0] in_1,
  output isJMP,
  output regWrite,
  output isLoad,
  output [2:0] ctrlUAL
);

  wire and_1_out, and_2_out, and_3_out, or_1_out;

  and and_1 (and_1_out, in_1[3], ~in_1[2]);  // AND_Gate
  and and_2 (and_2_out, in_1[3], in_1[2], ~in_1[1]);  // AND_Gate
  and and_3 (and_3_out, in_1[3], in_1[1], ~in_1[0]);  // AND_Gate
  or or_1 (or_1_out, and_3_out, and_2_out, and_1_out);
  and and_4 (isLoad, in_1[3], in_1[2], in_1[1], in_1[0]);
  Multiplexer #(.width(3)) multiplexer_1 (.in0(3'b001), .in1(in_1[2:0]), .out(ctrlUAL), .sel(or_1_out));  // open: en
  not not_1 (isJMP, in_1[3]);

  assign regWrite = in_1[3];
endmodule

module CtrlSaut (
  input  CF,
  input  ZF,
  input  SF,
  input  OF,
  input  [3:0] opcode,
  output [1:0] PC_ctrl
);

  wire and_1_out, and_2_out, and_3_out, and_4_out, and_5_out, and_6_out, and_7_out, and_8_out, halt_out,
       or_2_out, or_3_out;
  wire [1:1] or_1_out;

  and and_1 (and_1_out, ~ZF, ~opcode[2], opcode[1], ~opcode[0]);  // AND_Gate
  and and_2 (and_2_out, ZF, ~opcode[2], opcode[1], opcode[0]);  // AND_Gate
  and and_3 (and_3_out, opcode[2], ~opcode[1], ~opcode[0], ~ZF, SF);  // AND_Gate
  or or_1 (or_1_out[1], and_1_out, and_2_out, and_3_out, and_4_out, and_5_out, and_7_out, ~opcode[3]);  // OR_Gate
  and and_4 (and_4_out, opcode[2], ~opcode[1], opcode[0], ~ZF, ~SF);  // AND_Gate
  and and_5 (and_5_out, opcode[2], ~opcode[1], opcode[0], or_2_out);  // AND_Gate
  and and_6 (and_6_out, ~ZF, SF);  // AND_Gate
  or or_2 (or_2_out, and_6_out, ZF);
  and and_7 (and_7_out, opcode[2], opcode[1], opcode[0], or_3_out);
  and and_8 (and_8_out, ~ZF, ~SF);  // AND_Gate
  or or_3 (or_3_out, and_8_out, ZF);
  and halt (halt_out, ~opcode[3], ~opcode[2], ~opcode[1], ~opcode[0]);  // AND_Gate
  Multiplexer #(.width(2)) multiplexer_1 (
    .in0({or_1_out[1], 1'b1}), .in1(2'b00), .out(PC_ctrl), .sel(halt_out));  // open: en
endmodule

module BancRegistre (
  input  [7:0] valIn,
  input  [3:0] Rs,
  input  [3:0] Rt,
  input  [3:0] Rd,
  input  RESET,
  input  RegWrite,
  input  horloge
);

  wire and_1_out, and_2_out, and_3_out, and_4_out, and_5_out, and_6_out, and_7_out, and_8_out, and_9_out,
       and_10_out, and_11_out, and_12_out, and_13_out, and_14_out, and_15_out, and_16_out, r1, r2, r3, r4,
       r5, r6, r7, r8, r9, r10, r11, r12, r13, r14, r15, r16;

  SelRegistre selregistre_1 (
    .Rd(Rd), .r1(r1), .r2(r2), .r3(r3), .r4(r4), .r5(r5), .r6(r6), .r7(r7), .r8(r8), .r9(r9), .r10(r10),
    .r11(r11), .r12(r12), .r13(r13), .r14(r14), .r15(r15), .r16(r16));
  and and_1 (and_1_out, r2, RegWrite);
  and and_2 (and_2_out, r1, RegWrite);
  Register register_1 (.D(valIn), .en(and_1_out), .clk(horloge), .clr(RESET));  // open: Q
  Register register_2 (.D(valIn), .en(and_2_out), .clk(horloge), .clr(RESET));  // open: Q
  and and_3 (and_3_out, r4, RegWrite);
  and and_4 (and_4_out, r3, RegWrite);
  Register register_3 (.en(and_3_out), .clk(horloge), .clr(RESET));  // open: D, Q
  Register register_4 (.D(valIn), .en(and_4_out), .clk(horloge), .clr(RESET));  // open: Q
  and and_5 (and_5_out, r6, RegWrite);
  and and_6 (and_6_out, r5, RegWrite);
  Register register_5 (.D(valIn), .en(and_5_out), .clk(horloge), .clr(RESET));  // open: Q
  Register register_6 (.D(valIn), .en(and_6_out), .clk(horloge), .clr(RESET));  // open: Q
  Register register_7 (.D(valIn), .en(and_7_out), .clk(horloge), .clr(RESET));  // open: Q
  and and_7 (and_7_out, r8, RegWrite);
  Register register_8 (.D(valIn), .en(and_8_out), .clk(horloge), .clr(RESET));  // open: Q
  and and_8 (and_8_out, r7, RegWrite);
  and and_9 (and_9_out, r10, RegWrite);
  and and_10 (and_10_out, r9, RegWrite);
  Register register_9 (.D(valIn), .en(and_9_out), .clk(horloge), .clr(RESET));  // open: Q
  Register register_10 (.D(valIn), .en(and_10_out), .clk(horloge), .clr(RESET));  // open: Q
  and and_11 (and_11_out, r12, RegWrite);
  and and_12 (and_12_out, r11, RegWrite);
  Register register_11 (.D(valIn), .en(and_11_out), .clk(horloge), .clr(RESET));  // open: Q
  Register register_12 (.D(valIn), .en(and_12_out), .clk(horloge), .clr(RESET));  // open: Q
  and and_13 (and_13_out, r14, RegWrite);
  and and_14 (and_14_out, r13, RegWrite);
  Register register_13 (.D(valIn), .en(and_13_out), .clk(horloge), .clr(RESET));  // open: Q
  Register register_14 (.D(valIn), .en(and_14_out), .clk(horloge), .clr(RESET));  // open: Q
  and and_15 (and_15_out, r16, RegWrite);
  and and_16 (and_16_out, r15, RegWrite);
  Register register_15 (.D(valIn), .en(and_15_out), .clk(horloge), .clr(RESET));  // open: Q
  Register register_16 (.D(valIn), .en(and_16_out), .clk(horloge), .clr(RESET));  // open: Q
endmodule

module selectionReg (
  input  [3:0] Rd,
  input  [3:0] Rs,
  input  [3:0] Rt,
  input  isJump,
  output [3:0] Rs_Rt,
  output [3:0] Rd_Rt,
  output [3:0] RD_2
);

  Multiplexer #(.width(4)) multiplexer_1 (.in0(Rd), .in1(Rs), .out(Rd_Rt), .sel(isJump));  // open: en
  Multiplexer #(.width(4)) multiplexer_2 (.in0(Rs), .in1(Rt), .out(Rs_Rt), .sel(isJump));  // open: en

  assign RD_2 = Rd;
endmodule

module signExtender (
  input  [3:0] Input,
  output [7:0] Output
);


  assign Output = {{5{Input[3]}}, Input[2:0]};
endmodule

module Nono (
  input  Reset
);

  wire ual_1_cf, ual_1_of, ual_1_sf, ual_1_zf;
  wire [1:0] ctrlsaut_1_pc_ctrl;
  wire [7:0] adder_1_out, adder_2_out, counter_1_q, multiplexer_1_out, ual_1_out_8, undriven, undriven_2;

  Counter counter_1 (.D(multiplexer_1_out), .count(Reset), .Q(counter_1_q));  // open: load, carry, clk, clr
  Adder adder_1 (.a(counter_1_q), .b(8'h1), .out(adder_1_out));  // open: cin, cout
  UAL ual_1 (
    .RS(undriven), .RT(undriven_2), .CF(ual_1_cf), .ZF(ual_1_zf), .SF(ual_1_sf), .OF(ual_1_of),
    .out_8(ual_1_out_8));  // open: in_3
  Adder adder_2 (.a(adder_1_out), .out(adder_2_out));  // open: b, cin, cout
  CtrlSaut ctrlsaut_1 (
    .CF(ual_1_cf), .ZF(ual_1_zf), .SF(ual_1_sf), .OF(ual_1_of), .PC_ctrl(ctrlsaut_1_pc_ctrl));  // open: opcode
  Multiplexer #(.select(2), .width(8)) multiplexer_1 (
    .in0({8{1'b1}}), .in1(adder_2_out), .in3(adder_1_out), .out(multiplexer_1_out), .sel(ctrlsaut_1_pc_ctrl));  // open: in2, en
endmodule

module SelRegistre (
  input  [3:0] Rd,
  output r1,
  output r2,
  output r3,
  output r4,
  output r5,
  output r6,
  output r7,
  output r8,
  output r9,
  output r10,
  output r11,
  output r12,
  output r13,
  output r14,
  output r15,
  output r16
);

  and and_1 (r1, Rd[0], Rd[1], Rd[2], Rd[3]);
  and and_2 (r2, ~Rd[0], Rd[1], Rd[2], Rd[3]);  // AND_Gate
  and and_3 (r3, Rd[0], ~Rd[1], Rd[2], Rd[3]);  // AND_Gate
  and and_4 (r4, ~Rd[0], ~Rd[1], Rd[2], Rd[3]);  // AND_Gate
  and and_5 (r5, Rd[0], Rd[1], ~Rd[2], Rd[3]);  // AND_Gate
  and and_6 (r7, Rd[0], ~Rd[1], ~Rd[2], Rd[3]);  // AND_Gate
  and and_7 (r6, ~Rd[0], Rd[1], ~Rd[2], Rd[3]);  // AND_Gate
  and and_8 (r8, ~Rd[0], ~Rd[1], ~Rd[2], Rd[3]);  // AND_Gate
  and and_9 (r9, Rd[0], Rd[1], Rd[2], ~Rd[3]);  // AND_Gate
  and and_10 (r11, Rd[0], ~Rd[1], Rd[2], ~Rd[3]);  // AND_Gate
  and and_11 (r10, ~Rd[0], Rd[1], Rd[2], ~Rd[3]);  // AND_Gate
  and and_12 (r12, ~Rd[0], ~Rd[1], Rd[2], ~Rd[3]);  // AND_Gate
  and and_13 (r13, Rd[0], Rd[1], ~Rd[2], ~Rd[3]);  // AND_Gate
  and and_14 (r14, ~Rd[0], Rd[1], ~Rd[2], ~Rd[3]);  // AND_Gate
  and and_15 (r15, Rd[0], ~Rd[1], ~Rd[2], ~Rd[3]);  // AND_Gate
  and and_16 (r16, ~Rd[0], ~Rd[1], ~Rd[2], ~Rd[3]);  // AND_Gate
endmodule
