// Logisim project BR_selectRegistres.circ as structural Verilog: 1 circuit, main circuit main
module main (
  input  [3:0] Rd,
  output r15,
  output r14,
  output r13,
  output r12,
  output r11,
  output r10,
  output r9,
  output r8,
  output r7,
  output r6,
  output r5,
  output r4,
  output r3,
  output r2,
  output r1,
  output r0
);

  and and_1 (r15, Rd[0], Rd[1], Rd[2], Rd[3]);
  and and_2 (r13, Rd[0], ~Rd[1], Rd[2], Rd[3]);  // AND_Gate
  and and_3 (r14, ~Rd[0], Rd[1], Rd[2], Rd[3]);  // AND_Gate
  and and_4 (r12, ~Rd[0], ~Rd[1], Rd[2], Rd[3]);  // AND_Gate
  and and_5 (r11, Rd[0], Rd[1], ~Rd[2], Rd[3]);  // AND_Gate
  and and_6 (r10, ~Rd[0], Rd[1], ~Rd[2], Rd[3]);  // AND_Gate
  and and_7 (r9, Rd[0], ~Rd[1], ~Rd[2], Rd[3]);  // AND_Gate
  and and_8 (r8, ~Rd[0], ~Rd[1], ~Rd[2], Rd[3]);  // AND_Gate
  and and_9 (r7, Rd[0], Rd[1], Rd[2], ~Rd[3]);  // AND_Gate
  and and_10 (r6, ~Rd[0], Rd[1], Rd[2], ~Rd[3]);  // AND_Gate
  and and_11 (r5, Rd[0], ~Rd[1], Rd[2], ~Rd[3]);  // AND_Gate
  and and_12 (r4, ~Rd[0], ~Rd[1], Rd[2], ~Rd[3]);  // AND_Gate
  and and_13 (r3, Rd[0], Rd[1], ~Rd[2], ~Rd[3]);  // AND_Gate
  and and_14 (r2, ~Rd[0], Rd[1], ~Rd[2], ~Rd[3]);  // AND_Gate
  and and_15 (r1, Rd[0], ~Rd[1], ~Rd[2], ~Rd[3]);  // AND_Gate
  and and_16 (r0, ~Rd[0], ~Rd[1], ~Rd[2], ~Rd[3]);  // AND_Gate

  // Notes on the sheet:
  //   Cédric Bois, Sientzoff - Banc de registres : décondeur de nom de registres
endmodule
