// Logisim project Projet.circ as structural Verilog: 8 circuits, main circuit UAL
module Nono (
  input  Reset,
  output [7:0] t0,
  output [7:0] t1,
  output [7:0] out_4
);

  wire clock_1_out, decoder_instru_1_isjmp, decoder_instru_1_isload, decoder_instru_1_regwrite, ual_1_cf,
       ual_1_of, ual_1_sf, ual_1_zf;
  wire [1:0] ctrl_saut_pc_ctrl;
  wire [2:0] decoder_instru_1_ctrlual;
  wire [3:0] ram_1_data, selectionreg_1_rd, selectionreg_1_rs, selectionreg_1_rt_2;
  wire [7:0] adder_1_out, adder_2_out, bancregistre_1_rs_2, bancregistre_1_rt_2, multiplexer_2_out,
       register_1_q, signextender_1_output, ual_1_s;
  wire [11:0] ram_1_data_2;

  Clock clock_1 (.out(clock_1_out));
  Register register_1 (.D(multiplexer_2_out), .en(1'b1), .Q(register_1_q), .clk(clock_1_out), .clr(Reset));
  decoder_instru decoder_instru_1 (
    .in_1(ram_1_data), .isJMP(decoder_instru_1_isjmp), .regWrite(decoder_instru_1_regwrite),
    .isLoad(decoder_instru_1_isload), .ctrlUAL(decoder_instru_1_ctrlual));
  Adder adder_1 (.a(register_1_q), .b(8'h1), .out(adder_1_out));  // open: cin, cout
  RAM #(.dataWidth(16), .bus("asynch")) ram_1 (
    .addr(register_1_q), .data({ram_1_data, ram_1_data_2}));  // open: sel, ld, clr
  BancRegistre bancregistre_1 (
    .valIn(out_4), .rs(selectionreg_1_rs), .Rd(selectionreg_1_rd), .RESET(Reset),
    .RegWrite(decoder_instru_1_regwrite), .Rs_2(bancregistre_1_rs_2), .rt(selectionreg_1_rt_2),
    .Rt_2(bancregistre_1_rt_2), .horloge(clock_1_out), .out_9(t0), .out_10(t1));
  selectionReg selectionreg_1 (
    .isJump(decoder_instru_1_isjmp), .rt_2(selectionreg_1_rt_2), .rs(selectionreg_1_rs),
    .rd(selectionreg_1_rd), .Rd_Rs(ram_1_data_2[11:8]), .Rs_Rt(ram_1_data_2[7:4]), .Rt(ram_1_data_2[3:0]));
  Multiplexer #(.width(8)) multiplexer_1 (
    .in0(ual_1_s), .in1(ram_1_data_2[7:0]), .out(out_4), .sel(decoder_instru_1_isload));  // open: en
  Adder adder_2 (.a(adder_1_out), .b(signextender_1_output), .out(adder_2_out));  // open: cin, cout
  signExtender signextender_1 (.Input(ram_1_data_2[3:0]), .Output(signextender_1_output));
  UAL ual_1 (
    .RS(bancregistre_1_rs_2), .RT(bancregistre_1_rt_2), .in_3(decoder_instru_1_ctrlual), .CF(ual_1_cf),
    .ZF(ual_1_zf), .SF(ual_1_sf), .OF(ual_1_of), .S(ual_1_s));
  Multiplexer #(.select(2), .width(8)) multiplexer_2 (
    .in0({8{1'b1}}), .in1(adder_2_out), .in3(adder_1_out), .out(multiplexer_2_out), .sel(ctrl_saut_pc_ctrl));  // open: in2, en
  CtrlSaut ctrl_saut (
    .CF(ual_1_cf), .ZF(ual_1_zf), .SF(ual_1_sf), .OF(ual_1_of), .opcode(ram_1_data),
    .PC_ctrl(ctrl_saut_pc_ctrl));

  // Notes on the sheet:
  //   Bois Cédric, Sientzoff Benjamin - Processeur NONO 1
endmodule

module UAL (
  input  [7:0] RS,
  input  [7:0] RT,
  input  [2:0] in_3,
  output CF,
  output ZF,
  output SF,
  output OF,
  output [7:0] S
);

  wire adder_1_cout, and_1_out, and_2_out, and_3_out, and_5_out, subtractor_1_bout;
  wire [7:0] adder_1_out, and_4_out, not_1_out, or_1_out, shifter_1_out, shifter_2_out, subtractor_1_out;

  Subtractor subtractor_1 (.a(RS), .b(RT), .out(subtractor_1_out), .bout(subtractor_1_bout));  // open: bin
  Adder adder_1 (.a(RS), .b(RT), .out(adder_1_out), .cout(adder_1_cout));  // open: cin
  and and_1 (and_1_out, ~S[7], RS[7], ~RT[7], in_3[0]);  // AND_Gate
  assign or_1_out = RT | RS;  // OR_Gate or_1, 8 bits wide
  and and_2 (and_2_out, ~S[7], RS[7], RT[7], ~in_3[0]);  // AND_Gate
  Multiplexer #(.select(3), .width(8)) multiplexer_1 (
    .in0(adder_1_out), .in1(subtractor_1_out), .in2(or_1_out), .in3(and_4_out), .in4(not_1_out),
    .in5(shifter_1_out), .in6(shifter_2_out), .out(S), .sel(in_3));  // open: in7, en
  and and_3 (and_3_out, S[7], ~RS[7], ~RT[7], ~in_3[0]);  // AND_Gate
  or or_2 (OF, and_1_out, and_2_out, and_3_out, and_5_out);
  assign not_1_out = ~RS;  // NOT_Gate not_1, 8 bits wide
  assign and_4_out = RT & RS;  // AND_Gate and_4, 8 bits wide
  and and_5 (and_5_out, S[7], ~RS[7], RT[7], in_3[0]);  // AND_Gate
  Shifter shifter_1 (.in(RS), .\dist (RT[2:0]), .out(shifter_1_out));
  Multiplexer multiplexer_2 (.in0(adder_1_cout), .in1(subtractor_1_bout), .out(CF), .sel(in_3[0]));  // open: en
  Shifter #(.shift("lr")) shifter_2 (.in(RS), .\dist (RT[2:0]), .out(shifter_2_out));
  and and_6 (ZF, ~S[0], ~S[1], ~S[2], ~S[3], ~S[4], ~S[5], ~S[6], ~S[7]);  // AND_Gate

  assign SF = S[7];
endmodule

module decoder_instru (
  input  [3:0] in_1,
  output isJMP,
  output regWrite,
  output isLoad,
  output [2:0] ctrlUAL
);

  wire and_1_out, and_2_out, and_3_out, or_1_out;

  and and_1 (and_1_out, in_1[3], ~in_1[2]);  // AND_Gate
  and and_2 (and_2_out, in_1[3], in_1[2], ~in_1[1]);  // AND_Gate
  and and_3 (and_3_out, in_1[3], in_1[1], ~in_1[0]);  // AND_Gate
  or or_1 (or_1_out, and_3_out, and_2_out, and_1_out);
  and and_4 (isLoad, in_1[3], in_1[2], in_1[1], in_1[0]);
  Multiplexer #(.width(3)) multiplexer_1 (.in0(3'b001), .in1(in_1[2:0]), .out(ctrlUAL), .sel(or_1_out));  // open: en
  not not_1 (isJMP, in_1[3]);

  assign regWrite = in_1[3];
endmodule

module CtrlSaut (
  input  CF,
  input  OF,
  input  ZF,
  input  SF,
  input  [3:0] opcode,
  output [1:0] PC_ctrl
);

  wire and_1_out, and_2_out, and_3_out, and_4_out, and_5_out, and_6_out, and_7_out, and_8_out, halt_out,
       or_1_out, or_2_out, or_4_out;
  wire [1:1] or_3_out;

  and and_1 (and_1_out, ~ZF, ~opcode[2], opcode[1], ~opcode[0]);  // AND_Gate
  and and_2 (and_2_out, ZF, ~opcode[2], opcode[1], opcode[0]);  // AND_Gate
  and and_3 (and_3_out, opcode[2], ~opcode[1], ~opcode[0], ~ZF, SF);  // AND_Gate
  and and_4 (and_4_out, opcode[2], ~opcode[1], opcode[0], ~ZF, ~SF);  // AND_Gate
  and and_5 (and_5_out, opcode[2], opcode[1], ~opcode[0], or_2_out);  // AND_Gate
  or or_1 (or_1_out, and_1_out, and_2_out, and_3_out, and_4_out, and_5_out, and_7_out);
  and and_6 (and_6_out, ~ZF, SF);  // AND_Gate
  or or_2 (or_2_out, and_6_out, ZF);
  and and_7 (and_7_out, opcode[2], opcode[1], opcode[0], or_4_out);
  or or_3 (or_3_out[1], opcode[3], or_1_out);
  and and_8 (and_8_out, ~ZF, ~SF);  // AND_Gate
  or or_4 (or_4_out, and_8_out, ZF);
  and halt (halt_out, ~opcode[3], ~opcode[2], ~opcode[1], ~opcode[0]);  // AND_Gate
  Multiplexer #(.width(2)) multiplexer_1 (
    .in0({or_3_out[1], 1'b1}), .in1(2'b00), .out(PC_ctrl), .sel(halt_out));  // open: en
endmodule

module BancRegistre (
  input  [7:0] valIn,
  input  [3:0] rs,
  input  [3:0] rt,
  input  [3:0] Rd,
  input  RESET,
  input  RegWrite,
  input  horloge,
  output [7:0] Rs_2,
  output [7:0] out_9,
  output [7:0] out_10,
  output [7:0] Rt_2
);

  wire and_1_out, and_2_out, and_3_out, and_4_out, and_5_out, and_6_out, and_7_out, and_8_out, and_9_out,
       and_10_out, and_11_out, and_12_out, and_13_out, and_14_out, and_15_out, and_16_out, r0, r1, r2, r3,
       r4, r5, r6, r7, r8, r9, r10, r11, r12, r13, r14, r15;
  wire [7:0] register_2_q, register_4_q, register_5_q, register_6_q, register_7_q, register_8_q,
       register_9_q, register_10_q, register_11_q, register_12_q, register_13_q, register_14_q,
       register_15_q, register_16_q;

  SelRegistre selregistre_1 (
    .Rd(Rd), .r15(r15), .r14(r14), .r13(r13), .r12(r12), .r11(r11), .r10(r10), .r9(r9), .r8(r8), .r7(r7),
    .r6(r6), .r5(r5), .r4(r4), .r3(r3), .r2(r2), .r1(r1), .r0(r0));
  and and_1 (and_1_out, r0, RegWrite);
  and and_2 (and_2_out, r8, RegWrite);
  Register register_1 (.D(valIn), .en(and_1_out), .Q(out_9), .clk(horloge), .clr(RESET));
  Register register_2 (.D(valIn), .en(and_2_out), .Q(register_2_q), .clk(horloge), .clr(RESET));
  and and_3 (and_3_out, r1, RegWrite);
  and and_4 (and_4_out, r9, RegWrite);
  Register register_3 (.D(valIn), .en(and_3_out), .Q(out_10), .clk(horloge), .clr(RESET));
  Register register_4 (.D(valIn), .en(and_4_out), .Q(register_4_q), .clk(horloge), .clr(RESET));
  and and_5 (and_5_out, r2, RegWrite);
  and and_6 (and_6_out, r10, RegWrite);
  Register register_5 (.D(valIn), .en(and_5_out), .Q(register_5_q), .clk(horloge), .clr(RESET));
  Register register_6 (.D(valIn), .en(and_6_out), .Q(register_6_q), .clk(horloge), .clr(RESET));
  Register register_7 (.D(valIn), .en(and_7_out), .Q(register_7_q), .clk(horloge), .clr(RESET));
  and and_7 (and_7_out, r3, RegWrite);
  Register register_8 (.D(valIn), .en(and_8_out), .Q(register_8_q), .clk(horloge), .clr(RESET));
  and and_8 (and_8_out, r11, RegWrite);
  and and_9 (and_9_out, r4, RegWrite);
  and and_10 (and_10_out, r12, RegWrite);
  Register register_9 (.D(valIn), .en(and_9_out), .Q(register_9_q), .clk(horloge), .clr(RESET));
  Register register_10 (.D(valIn), .en(and_10_out), .Q(register_10_q), .clk(horloge), .clr(RESET));
  and and_11 (and_11_out, r5, RegWrite);
  and and_12 (and_12_out, r13, RegWrite);
  Register register_11 (.D(valIn), .en(and_11_out), .Q(register_11_q), .clk(horloge), .clr(RESET));
  Register register_12 (.D(valIn), .en(and_12_out), .Q(register_12_q), .clk(horloge), .clr(RESET));
  and and_13 (and_13_out, r6, RegWrite);
  and and_14 (and_14_out, r14, RegWrite);
  Register register_13 (.D(valIn), .en(and_13_out), .Q(register_13_q), .clk(horloge), .clr(RESET));
  Register register_14 (.D(valIn), .en(and_14_out), .Q(register_14_q), .clk(horloge), .clr(RESET));
  and and_15 (and_15_out, r7, RegWrite);
  and and_16 (and_16_out, r15, RegWrite);
  Register register_15 (.D(valIn), .en(and_15_out), .Q(register_15_q), .clk(horloge), .clr(RESET));
  Register register_16 (.D(valIn), .en(and_16_out), .Q(register_16_q), .clk(horloge), .clr(RESET));
  Multiplexer #(.select(4), .width(8)) multiplexer_1 (
    .in0(out_9), .in1(out_10), .in2(register_5_q), .in3(register_7_q), .in4(register_9_q),
    .in5(register_11_q), .in6(register_13_q), .in7(register_15_q), .in8(register_16_q), .in9(register_14_q),
    .in10(register_12_q), .in11(register_10_q), .in12(register_8_q), .in13(register_6_q),
    .in14(register_4_q), .in15(register_2_q), .out(Rt_2), .sel(rt));  // open: en
  Multiplexer #(.select(4), .width(8)) multiplexer_2 (
    .in0(out_9), .in1(out_10), .in2(register_5_q), .in3(register_7_q), .in4(register_9_q),
    .in5(register_11_q), .in6(register_13_q), .in7(register_15_q), .in8(register_16_q), .in9(register_14_q),
    .in10(register_12_q), .in11(register_10_q), .in12(register_8_q), .in13(register_6_q),
    .in14(register_4_q), .in15(register_2_q), .out(Rs_2), .sel(rs));  // open: en
endmodule

module selectionReg (
  input  [3:0] Rd_Rs,
  input  [3:0] Rs_Rt,
  input  [3:0] Rt,
  input  isJump,
  output [3:0] rt_2,
  output [3:0] rs,
  output [3:0] rd
);

  Multiplexer #(.width(4)) multiplexer_1 (.in0(Rs_Rt), .in1(Rd_Rs), .out(rs), .sel(isJump));  // open: en
  Multiplexer #(.width(4)) multiplexer_2 (.in0(Rt), .in1(Rs_Rt), .out(rt_2), .sel(isJump));  // open: en

  assign rd = Rd_Rs;
endmodule

module signExtender (
  input  [3:0] Input,
  output [7:0] Output
);


  assign Output = {{5{Input[3]}}, Input[2:0]};
endmodule

module SelRegistre (
  input  [3:0] Rd,
  output r15,
  output r14,
  output r13,
  output r12,
  output r11,
  output r10,
  output r9,
  output r8,
  output r7,
  output r6,
  output r5,
  output r4,
  output r3,
  output r2,
  output r1,
  output r0
);

  and and_1 (r15, Rd[0], Rd[1], Rd[2], Rd[3]);
  and and_2 (r13, Rd[0], ~Rd[1], Rd[2], Rd[3]);  // AND_Gate
  and and_3 (r14, ~Rd[0], Rd[1], Rd[2], Rd[3]);  // AND_Gate
  and and_4 (r12, ~Rd[0], ~Rd[1], Rd[2], Rd[3]);  // AND_Gate
  and and_5 (r11, Rd[0], Rd[1], ~Rd[2], Rd[3]);  // AND_Gate
  and and_6 (r9, Rd[0], ~Rd[1], ~Rd[2], Rd[3]);  // AND_Gate
  and and_7 (r10, ~Rd[0], Rd[1], ~Rd[2], Rd[3]);  // AND_Gate
  and and_8 (r8, ~Rd[0], ~Rd[1], ~Rd[2], Rd[3]);  // AND_Gate
  and and_9 (r7, Rd[0], Rd[1], Rd[2], ~Rd[3]);  // AND_Gate
  and and_10 (r6, ~Rd[0], Rd[1], Rd[2], ~Rd[3]);  // AND_Gate
  and and_11 (r5, Rd[0], ~Rd[1], Rd[2], ~Rd[3]);  // AND_Gate
  and and_12 (r4, ~Rd[0], ~Rd[1], Rd[2], ~Rd[3]);  // AND_Gate
  and and_13 (r3, Rd[0], Rd[1], ~Rd[2], ~Rd[3]);  // AND_Gate
  and and_14 (r1, Rd[0], ~Rd[1], ~Rd[2], ~Rd[3]);  // AND_Gate
  and and_15 (r2, ~Rd[0], Rd[1], ~Rd[2], ~Rd[3]);  // AND_Gate
  and and_16 (r0, ~Rd[0], ~Rd[1], ~Rd[2], ~Rd[3]);  // AND_Gate
endmodule
