// Logisim project UAL.circ as structural Verilog: 1 circuit, main circuit main
module main (
  input  [7:0] RS,
  input  [7:0] RT,
  input  [2:0] ctrlUAL,
  output ZF,
  output CF,
  output SF,
  output [7:0] \output ,
  output OF
);

  wire adder_1_cout, and_1_out, and_2_out, and_4_out, and_5_out, subtractor_1_bout;
  wire [7:0] adder_1_out, and_3_out, not_1_out, or_1_out, shifter_1_out, shifter_2_out, subtractor_1_out;

  Subtractor subtractor_1 (.a(RS), .b(RT), .out(subtractor_1_out), .bout(subtractor_1_bout));  // open: bin
  Adder adder_1 (.a(RS), .b(RT), .out(adder_1_out), .cout(adder_1_cout));  // open: cin
  and and_1 (and_1_out, ~\output [7], RS[7], ~RT[7], ctrlUAL[0]);  // AND_Gate
  assign or_1_out = RT | RS;  // OR_Gate or_1, 8 bits wide
  Multiplexer multiplexer_1 (.in0(adder_1_cout), .in1(subtractor_1_bout), .out(CF), .sel(ctrlUAL[0]));  // open: en
  and and_2 (and_2_out, ~\output [7], RS[7], RT[7], ~ctrlUAL[0]);  // AND_Gate
  assign and_3_out = RT & RS;  // AND_Gate and_3, 8 bits wide
  Multiplexer #(.select(3), .width(8)) multiplexer_2 (
    .in0(adder_1_out), .in1(subtractor_1_out), .in2(or_1_out), .in3(and_3_out), .in4(not_1_out),
    .in5(shifter_2_out), .in6(shifter_1_out), .out(\output ), .sel(ctrlUAL));  // open: in7, en
  and and_4 (and_4_out, \output [7], ~RS[7], ~RT[7], ~ctrlUAL[0]);  // AND_Gate
  or or_2 (OF, and_1_out, and_2_out, and_4_out, and_5_out);
  assign not_1_out = ~RS;  // NOT_Gate not_1, 8 bits wide
  and and_5 (and_5_out, \output [7], ~RS[7], RT[7], ctrlUAL[0]);  // AND_Gate
  Shifter #(.shift("lr")) shifter_1 (.in(RS), .\dist (RT[2:0]), .out(shifter_1_out));
  Shifter shifter_2 (.in(RS), .\dist (RT[2:0]), .out(shifter_2_out));
  and and_6 (ZF, ~\output [0], ~\output [1], ~\output [2], ~\output [3], ~\output [4], ~\output [5], ~\output [6], ~\output [7]);  // AND_Gate

  assign SF = \output [7];

  // Notes on the sheet:
  //   Cédric Bois, Benjamin Sientzoff - UAL
endmodule
