// Logisim project banc_regist.circ as structural Verilog: 2 circuits, main circuit main
module main (
  input  [7:0] valIn,
  input  [3:0] rs,
  input  [3:0] rt,
  input  RESET,
  input  RegWrite,
  input  [3:0] Rd,
  input  horloge,
  output [7:0] out_8,
  output [7:0] out_9,
  output [7:0] Rs_2,
  output [7:0] Rt_2
);

  wire and_1_out, and_2_out, and_3_out, and_4_out, and_5_out, and_6_out, and_7_out, and_8_out, and_9_out,
       and_10_out, and_11_out, and_12_out, and_13_out, and_14_out, and_15_out, and_16_out, r1, r2, r3, r4,
       r5, r6, r7, r8, r9, r10, r11, r12, r13, r14, r15, r16;
  wire [7:0] register_2_q, register_4_q, register_5_q, register_6_q, register_7_q, register_8_q,
       register_9_q, register_10_q, register_11_q, register_12_q, register_13_q, register_14_q,
       register_15_q, register_16_q;

  and and_1 (and_1_out, r1, RegWrite);
  and and_2 (and_2_out, r9, RegWrite);
  Register register_1 (.D(valIn), .en(and_1_out), .Q(out_8), .clk(horloge), .clr(RESET));
  Register register_2 (.D(valIn), .en(and_2_out), .Q(register_2_q), .clk(horloge), .clr(RESET));
  BC_sel_reg bc_sel_reg_1 (
    .Rd(Rd), .r1(r16), .r2(r15), .r3(r14), .r4(r13), .r5(r12), .r6(r11), .r7(r10), .r8(r9), .r9(r8),
    .r10(r7), .r11(r6), .r12(r5), .r13(r4), .r14(r3), .r15(r2), .r16(r1));
  and and_3 (and_3_out, r2, RegWrite);
  and and_4 (and_4_out, r10, RegWrite);
  Register register_3 (.D(valIn), .en(and_3_out), .Q(out_9), .clk(horloge), .clr(RESET));
  Register register_4 (.D(valIn), .en(and_4_out), .Q(register_4_q), .clk(horloge), .clr(RESET));
  and and_5 (and_5_out, r3, RegWrite);
  and and_6 (and_6_out, r11, RegWrite);
  Register register_5 (.D(valIn), .en(and_5_out), .Q(register_5_q), .clk(horloge), .clr(RESET));
  Register register_6 (.D(valIn), .en(and_6_out), .Q(register_6_q), .clk(horloge), .clr(RESET));
  Register register_7 (.D(valIn), .en(and_7_out), .Q(register_7_q), .clk(horloge), .clr(RESET));
  and and_7 (and_7_out, r4, RegWrite);
  Register register_8 (.D(valIn), .en(and_8_out), .Q(register_8_q), .clk(horloge), .clr(RESET));
  and and_8 (and_8_out, r12, RegWrite);
  and and_9 (and_9_out, r5, RegWrite);
  and and_10 (and_10_out, r13, RegWrite);
  Register register_9 (.D(valIn), .en(and_9_out), .Q(register_9_q), .clk(horloge), .clr(RESET));
  Register register_10 (.D(valIn), .en(and_10_out), .Q(register_10_q), .clk(horloge), .clr(RESET));
  and and_11 (and_11_out, r6, RegWrite);
  and and_12 (and_12_out, r14, RegWrite);
  Register register_11 (.D(valIn), .en(and_11_out), .Q(register_11_q), .clk(horloge), .clr(RESET));
  Register register_12 (.D(valIn), .en(and_12_out), .Q(register_12_q), .clk(horloge), .clr(RESET));
  and and_13 (and_13_out, r7, RegWrite);
  and and_14 (and_14_out, r15, RegWrite);
  Register register_13 (.D(valIn), .en(and_13_out), .Q(register_13_q), .clk(horloge), .clr(RESET));
  Register register_14 (.D(valIn), .en(and_14_out), .Q(register_14_q), .clk(horloge), .clr(RESET));
  and and_15 (and_15_out, r8, RegWrite);
  and and_16 (and_16_out, r16, RegWrite);
  Register register_15 (.D(valIn), .en(and_15_out), .Q(register_15_q), .clk(horloge), .clr(RESET));
  Register register_16 (.D(valIn), .en(and_16_out), .Q(register_16_q), .clk(horloge), .clr(RESET));
  Multiplexer #(.select(4), .width(8)) multiplexer_1 (
    .in0(out_8), .in1(out_9), .in2(register_5_q), .in3(register_7_q), .in4(register_9_q),
    .in5(register_11_q), .in6(register_13_q), .in7(register_15_q), .in8(register_16_q), .in9(register_14_q),
    .in10(register_12_q), .in11(register_10_q), .in12(register_8_q), .in13(register_6_q),
    .in14(register_4_q), .in15(register_2_q), .out(Rt_2), .sel(rt));  // open: en
  Multiplexer #(.select(4), .width(8)) multiplexer_2 (
    .in0(out_8), .in1(out_9), .in2(register_5_q), .in3(register_7_q), .in4(register_9_q),
    .in5(register_11_q), .in6(register_13_q), .in7(register_15_q), .in8(register_16_q), .in9(register_14_q),
    .in10(register_12_q), .in11(register_10_q), .in12(register_8_q), .in13(register_6_q),
    .in14(register_4_q), .in15(register_2_q), .out(Rs_2), .sel(rs));  // open: en

  // Notes on the sheet:
  //   Bois Cédric, Sientzoff Benjamin - Banc de registres
endmodule

module BC_sel_reg (
  input  [3:0] Rd,
  output r1,
  output r2,
  output r3,
  output r4,
  output r5,
  output r6,
  output r7,
  output r8,
  output r9,
  output r10,
  output r11,
  output r12,
  output r13,
  output r14,
  output r15,
  output r16
);

  and and_1 (r1, Rd[0], Rd[1], Rd[2], Rd[3]);
  and and_2 (r3, Rd[0], ~Rd[1], Rd[2], Rd[3]);  // AND_Gate
  and and_3 (r2, ~Rd[0], Rd[1], Rd[2], Rd[3]);  // AND_Gate
  and and_4 (r4, ~Rd[0], ~Rd[1], Rd[2], Rd[3]);  // AND_Gate
  and and_5 (r5, Rd[0], Rd[1], ~Rd[2], Rd[3]);  // AND_Gate
  and and_6 (r6, ~Rd[0], Rd[1], ~Rd[2], Rd[3]);  // AND_Gate
  and and_7 (r7, Rd[0], ~Rd[1], ~Rd[2], Rd[3]);  // AND_Gate
  and and_8 (r8, ~Rd[0], ~Rd[1], ~Rd[2], Rd[3]);  // AND_Gate
  and and_9 (r9, Rd[0], Rd[1], Rd[2], ~Rd[3]);  // AND_Gate
  and and_10 (r11, Rd[0], ~Rd[1], Rd[2], ~Rd[3]);  // AND_Gate
  and and_11 (r10, ~Rd[0], Rd[1], Rd[2], ~Rd[3]);  // AND_Gate
  and and_12 (r12, ~Rd[0], ~Rd[1], Rd[2], ~Rd[3]);  // AND_Gate
  and and_13 (r13, Rd[0], Rd[1], ~Rd[2], ~Rd[3]);  // AND_Gate
  and and_14 (r15, Rd[0], ~Rd[1], ~Rd[2], ~Rd[3]);  // AND_Gate
  and and_15 (r14, ~Rd[0], Rd[1], ~Rd[2], ~Rd[3]);  // AND_Gate
  and and_16 (r16, ~Rd[0], ~Rd[1], ~Rd[2], ~Rd[3]);  // AND_Gate
endmodule
