// Logisim project decodeurInstru.circ as structural Verilog: 1 circuit, main circuit main
module main (
  input  [3:0] in_1,
  output isJMP,
  output regWrite,
  output isLoad,
  output [2:0] ctrlUAL
);

  wire and_1_out, and_2_out, and_3_out, or_1_out;

  and and_1 (and_1_out, in_1[3], ~in_1[2]);  // AND_Gate
  and and_2 (and_2_out, in_1[3], in_1[2], ~in_1[1]);  // AND_Gate
  and and_3 (and_3_out, in_1[3], in_1[1], ~in_1[0]);  // AND_Gate
  or or_1 (or_1_out, and_3_out, and_2_out, and_1_out);
  and and_4 (isLoad, in_1[3], in_1[2], in_1[1], in_1[0]);
  Multiplexer #(.width(3)) multiplexer_1 (.in0(3'b001), .in1(in_1[2:0]), .out(ctrlUAL), .sel(or_1_out));  // open: en
  not not_1 (isJMP, in_1[3]);

  assign regWrite = in_1[3];

  // Notes on the sheet:
  //   Cédric Bois,  Sientzoff - Décodeur d'instruction
endmodule
