// Logisim project selectRegistres.circ as structural Verilog: 1 circuit, main circuit main
module main (
  input  [3:0] Rd_Rs,
  input  [3:0] Rs_Rt,
  input  [3:0] Rt,
  input  isJump,
  output [3:0] rt_2,
  output [3:0] rd,
  output [3:0] rs
);

  Multiplexer #(.width(4)) multiplexer_1 (.in0(Rs_Rt), .in1(Rd_Rs), .out(rs), .sel(isJump));  // open: en
  Multiplexer #(.width(4)) multiplexer_2 (.in0(Rt), .in1(Rs_Rt), .out(rt_2), .sel(isJump));  // open: en

  assign rd = Rd_Rs;

  // Notes on the sheet:
  //   Cédric Bois,  Sientzoff - Sélection de registres
endmodule
